# Fritzing sketch SmartCar (saved by Fritzing 0.9.3b)

parts:
  Arduino_Mega = Arduino Mega 2560 (Rev3)
  Bluetooth_module = Bluetooth HC-05 Macho
  Left = SRF05 Ultrasonic Rangefinder
  Mid-Left = SRF05 Ultrasonic Rangefinder
  Right = SRF05 Ultrasonic Rangefinder
  Rear = SRF05 Ultrasonic Rangefinder
  Mid-Right = SRF05 Ultrasonic Rangefinder
  Mid = SRF05 Ultrasonic Rangefinder
  Voltage_sensor = Voltage Sensor Module
  Battery_pack = 4 x AAA Battery Mount

nets:
  N1: Arduino_Mega.A0, Voltage_sensor.OUT
  N2: Arduino_Mega.D15/RX3, Bluetooth_module.TXD
  N3: Arduino_Mega.D14/TX3, Bluetooth_module.RXD
  N4: Arduino_Mega.D42, Rear.Echo
  N5: Arduino_Mega.D43, Rear.Trig
  N6: Arduino_Mega.D44, Left.Echo
  N7: Arduino_Mega.D45, Left.Trig
  N8: Arduino_Mega.D46, Mid-Left.Echo
  N9: Arduino_Mega.D47, Mid-Left.Trig
  N10: Arduino_Mega.D48, Mid.Echo
  N11: Arduino_Mega.D49, Mid.Trig
  N12: Arduino_Mega.D50, Mid-Right.Echo
  N13: Arduino_Mega.D51, Mid-Right.Trig
  N14: Arduino_Mega.D52, Right.Echo
  N15: Arduino_Mega.D53, Right.Trig
  N16: Voltage_sensor.INPUT+, Battery_pack.+
  N17: Voltage_sensor.INPUT-, Battery_pack.-

notes:
  Ultrasonic sensor
  Sensor Arduino (Trigger/Echo)
  Right 53/52 (digital)
  Mid-Right 51/50 (digital)
  Mid 49/48 (digital)
  Mid-Left 47/46 (digital)
  Left 45/44 (digital)
  Rear 43/42 (digital)
  GND GND
  VCC 5 V
  Bluetooth module
  Module Arduino(communication)
  TXD RX3/15
  RXD TX3/14
  GND GND
  VCC 5 V
  Voltage sensor
  Sensor Arduino
  S A0 (analog in)
  - GND
  Sensor Batterypack
  GND Negative terminal
  VCC Positive terminal
